# Fritzing sketch circuit_diagram (saved by Fritzing 0.9.3b)
breadboards: 1

parts:
  Raspberry_Pi1 = Raspberry Pi 2
  LED1 = LED - 5mm [color="Yellow (595nm)" package="5 mm [THT]"]
  R1 = Resistor [tolerance=±5% resistance=330 package=THT]
  LED2 = LED - 5mm [color="Red (633nm)" package="5 mm [THT]"]
  R2 = Resistor [tolerance=±5% resistance=220 package=THT]
  WeMos_D1_Mini_Relay_Shield_V1 = WeMos D1 Mini Relay Shield V2

nets:
  N1: Raspberry_Pi1.GPIO25, LED2.anode
  N2: Raspberry_Pi1.GND, R1.Pin_0, R2.Pin_0, WeMos_D1_Mini_Relay_Shield_V1.G
  N3: Raspberry_Pi1.GPIO24, WeMos_D1_Mini_Relay_Shield_V1.D1
  N4: Raspberry_Pi1.GPIO18, LED1.anode
  5V: Raspberry_Pi1.5V, WeMos_D1_Mini_Relay_Shield_V1.5V
  N5: LED1.cathode, R1.Pin_1
  N6: LED2.cathode, R2.Pin_1
